// Logisim project logisim-week_4.circ as structural Verilog: 1 circuit, main circuit main
module main (
  input  a,
  input  b,
  input  c,
  input  d,
  output x,
  output y,
  output z,
  output u,
  output v,
  output w,
  output s
);

  wire and_1_out, and_2_out, and_3_out, and_4_out, and_5_out, and_6_out, and_7_out, and_8_out, and_9_out,
       and_10_out, and_11_out, and_12_out, and_13_out, and_14_out, and_15_out, and_16_out, not_1_out,
       not_2_out, not_3_out, not_4_out, not_5_out, not_6_out, not_7_out, not_8_out, not_9_out, not_10_out,
       not_11_out, not_12_out, not_13_out, not_14_out, not_15_out, not_16_out, not_17_out, not_18_out,
       not_19_out, not_20_out, not_21_out;

  not not_1 (not_1_out, b);
  not not_2 (not_2_out, c);
  and and_1 (and_1_out, not_2_out, not_3_out);
  not not_3 (not_3_out, d);
  and and_2 (and_2_out, c, d);
  not not_4 (not_4_out, b);
  and and_3 (and_3_out, not_4_out, not_5_out);
  not not_5 (not_5_out, d);
  and and_4 (and_4_out, b, d);
  not not_6 (not_6_out, c);
  and and_5 (and_5_out, not_6_out, not_7_out);
  not not_7 (not_7_out, d);
  and and_6 (and_6_out, b, not_8_out);
  not not_8 (not_8_out, c);
  and and_7 (and_7_out, b, not_9_out);
  not not_9 (not_9_out, d);
  not not_10 (not_10_out, b);
  and and_8 (and_8_out, not_10_out, c);
  and and_9 (and_9_out, b, not_11_out);
  not not_11 (not_11_out, c);
  and and_10 (and_10_out, b, not_12_out);
  not not_12 (not_12_out, d);
  not not_13 (not_13_out, c);
  or or_1 (v, not_13_out, d, b);
  not not_14 (not_14_out, b);
  and and_11 (and_11_out, not_14_out, not_15_out);
  not not_15 (not_15_out, d);
  not not_16 (not_16_out, b);
  and and_12 (and_12_out, not_16_out, c);
  and and_13 (and_13_out, c, not_17_out);
  not not_17 (not_17_out, d);
  and and_14 (and_14_out, b, not_18_out, d);
  not not_18 (not_18_out, c);
  not not_19 (not_19_out, b);
  and and_15 (and_15_out, not_19_out, not_20_out);
  not not_20 (not_20_out, d);
  and and_16 (and_16_out, c, not_21_out);
  not not_21 (not_21_out, d);
  or or_2 (x, not_1_out, and_1_out, and_2_out);
  or or_3 (y, and_3_out, c, and_4_out);
  or or_4 (z, and_5_out, and_6_out, and_7_out);
  or or_5 (u, and_8_out, and_9_out, and_10_out, a);
  or or_6 (w, and_11_out, and_12_out, and_13_out, and_14_out);
  or or_7 (s, and_15_out, and_16_out);
  _7_Segment_Display u_7_segment_display_1 (.g(u), .f(z), .a(y), .b(x), .e(s), .d(w), .c(v));  // open: dp
endmodule
